# Fritzing sketch Solarcar_SFZ_FN_High_Current (saved by Fritzing 1.0.3b)
breadboards: 1

parts:
  Energy_storage/_BMS = DC Power [voltage=48V internal_resistance=0.1Ω]
  Motor_controller = HEZHU BLDC 3-Phase DC motor controller
  Motor = 3phase motor with hall sensors
  Forward/_backward = Toggle Switch [package=THT]
  Accelerator_pedal = Rotary Potentiometer (Small) [maximum_resistance=10kΩ knob_status=50% power=0.5W package=THT]
  ON/_OFF = Toggle Switch [package=THT]
  Fuse_300A = FUSE [package=fuse_5mm]
  MPPT_Solar_charge_controller1 = Drok DC buck module
  Solar_Panel1 = Solar Panel [package="Renogy 50 Watts 12 Volt Monocrystalline Bendable Solar Panel"]
  Solar_Panel2 = Solar Panel [package="Renogy 50 Watts 12 Volt Monocrystalline Bendable Solar Panel"]
  MPPT_Solar_charge_controller2 = Drok DC buck module
  Solar_Panel3 = Solar Panel [package="Renogy 50 Watts 12 Volt Monocrystalline Bendable Solar Panel"]
  Solar_Panel4 = Solar Panel [package="Renogy 50 Watts 12 Volt Monocrystalline Bendable Solar Panel"]
  + = BANANA_CONN [package=banana_conn]
  - = BANANA_CONN [package=banana_conn]
  ON/OFF = Toggle Switch [package=THT]
  ON/OFF_2 = Toggle Switch [package=THT]
  Emergency_electrical_isolation = Toggle Switch [package=THT]
  R1 = Resistor [tolerance=±5% power=0.25W resistance=0 package=THT]
  R2 = Resistor [tolerance=±5% power=0.25W resistance=0 package=THT]

nets:
  N1: Energy_storage/_BMS.V-, Fuse_300A.1, -.1
  N2: Energy_storage/_BMS.V+, Motor_controller.Pin_20, MPPT_Solar_charge_controller1.Pin_3, MPPT_Solar_charge_controller2.Pin_3, +.1
  N3: Motor_controller.Pin_6, Motor_controller.Pin_21, Forward/_backward.COM, Fuse_300A.2, MPPT_Solar_charge_controller1.Pin_1, MPPT_Solar_charge_controller1.Pin_4, Solar_Panel2.Connector_2, MPPT_Solar_charge_controller2.Pin_1, MPPT_Solar_charge_controller2.Pin_4, Solar_Panel4.Connector_2
  N4: Motor_controller.Pin_7, Motor.Pin_6
  N5: Motor_controller.Pin_8, Motor.Pin_5
  N6: Motor_controller.Pin_9, Motor.Pin_4
  N7: Motor_controller.Pin_13, Forward/_backward.L1
  N8: Motor_controller.Pin_14, Accelerator_pedal.leg2
  N9: Motor_controller.Pin_15, Accelerator_pedal.wiper
  N10: Motor_controller.Pin_16, Accelerator_pedal.leg1
  N11: Motor_controller.Pin_17, Motor.Pin_1
  N12: Motor_controller.Pin_18, Motor.Pin_2
  N13: Motor_controller.Pin_19, Motor.Pin_3
  N14: ON/_OFF.COM, R2.Pin_0
  N15: MPPT_Solar_charge_controller1.Pin_2, Solar_Panel1.Connector_1
  N16: Solar_Panel1.Connector_2, Solar_Panel2.Connector_1
  N17: MPPT_Solar_charge_controller2.Pin_2, Solar_Panel3.Connector_1
  N18: Solar_Panel3.Connector_2, Solar_Panel4.Connector_1
  N19: ON/OFF.COM, ON/OFF_2.L1
  N20: ON/OFF_2.COM, Emergency_electrical_isolation.L1
  N21: Emergency_electrical_isolation.COM, R1.Pin_0

notes:
  SolarCar SFZ Friedrichshafen, Simplified wiring diagram for iLumen European Solar Challenge. Component symbols are valid.
  48V
  Charger input
  Energy storage pack

custom parts:
  HEZHU BLDC 3-Phase DC motor controller: HEZHU BLDC 3-Phase DC 6V-60V 400W Brushless Motor Controller PWM Hall Motor Control.
  3phase motor with hall sensors: 3phase motor with hall sensors.
  Solar Panel: Renogy 50 Watts 12 Volt Solar Panel
