# Fritzing sketch Solarcar_SFZ_FN_High_Current_2 (saved by Fritzing 1.0.3b)
breadboards: 1

parts:
  Energy_storage/_BMS = DC Power [voltage=48V internal_resistance=0.1Ω]
  Motor_controller = HEZHU BLDC 3-Phase DC motor controller
  Motor = 3phase motor with hall sensors
  Forward/_backward = Toggle Switch [package=THT]
  Accelerator_pedal = Rotary Potentiometer (Small) [maximum_resistance=10kΩ knob_status=50% power=0.5W package=THT]
  ON/_OFF = Toggle Switch [package=THT]
  MPPT_Solar_charge_controller1 = Drok DC buck module
  Solar_Panel1 = Solar Panel [package="Renogy 50 Watts 12 Volt Monocrystalline Bendable Solar Panel"]
  Solar_Panel2 = Solar Panel [package="Renogy 50 Watts 12 Volt Monocrystalline Bendable Solar Panel"]
  MPPT_Solar_charge_controller2 = Drok DC buck module
  Solar_Panel3 = Solar Panel [package="Renogy 50 Watts 12 Volt Monocrystalline Bendable Solar Panel"]
  Solar_Panel4 = Solar Panel [package="Renogy 50 Watts 12 Volt Monocrystalline Bendable Solar Panel"]
  + = BANANA_CONN [package=banana_conn]
  - = BANANA_CONN [package=banana_conn]
  ON/OFF = Toggle Switch [package=THT]
  ON/OFF_2 = Toggle Switch [package=THT]
  Emergency_electrical_isolation_-_contact1 = Toggle Switch [package=THT]
  R1 = Resistor [tolerance=±5% power=0.25W resistance=0 package=THT]
  R2 = Resistor [tolerance=±5% power=0.25W resistance=0 package=THT]
  Fuse_300A = FUSE [package=fuse_5mm]
  M2 = 1 chan 5v relay module
  M3 = 1 chan 5v relay module
  Emergency_electrical_isolation_-_contact2 = Toggle Switch [package=THT]

nets:
  N1: Energy_storage/_BMS.V-, Motor_controller.Pin_6, Motor_controller.Pin_21, Forward/_backward.COM, MPPT_Solar_charge_controller1.Pin_1, MPPT_Solar_charge_controller1.Pin_4, Solar_Panel2.Connector_2, MPPT_Solar_charge_controller2.Pin_1, MPPT_Solar_charge_controller2.Pin_4, Solar_Panel4.Connector_2, -.1, M2.pin_2, M2.pin_6, M3.pin_2, M3.pin_6
  N2: Energy_storage/_BMS.V+, +.1, Fuse_300A.1
  N3: Motor_controller.Pin_7, Motor.Pin_6
  N4: Motor_controller.Pin_8, Motor.Pin_5
  N5: Motor_controller.Pin_9, Motor.Pin_4
  N6: Motor_controller.Pin_13, Forward/_backward.L1
  N7: Motor_controller.Pin_14, Accelerator_pedal.leg2
  N8: Motor_controller.Pin_15, Accelerator_pedal.wiper
  N9: Motor_controller.Pin_16, Accelerator_pedal.leg1
  N10: Motor_controller.Pin_17, Motor.Pin_1
  N11: Motor_controller.Pin_18, Motor.Pin_2
  N12: Motor_controller.Pin_19, Motor.Pin_3
  N13: Motor_controller.Pin_20, MPPT_Solar_charge_controller1.Pin_3, MPPT_Solar_charge_controller2.Pin_3, Fuse_300A.2, Emergency_electrical_isolation_-_contact2.COM
  N14: ON/_OFF.COM, R2.Pin_0
  N15: MPPT_Solar_charge_controller1.Pin_2, Solar_Panel1.Connector_1, M2.pin_5
  N16: Solar_Panel1.Connector_2, Solar_Panel2.Connector_1
  N17: MPPT_Solar_charge_controller2.Pin_2, Solar_Panel3.Connector_1, M3.pin_5
  N18: Solar_Panel3.Connector_2, Solar_Panel4.Connector_1
  N19: ON/OFF.L1, ON/OFF_2.COM
  N20: ON/OFF_2.L1, Emergency_electrical_isolation_-_contact1.COM
  N21: Emergency_electrical_isolation_-_contact1.L1, R1.Pin_0
  N22: M2.pin_1, M3.pin_1, Emergency_electrical_isolation_-_contact2.L1

notes:
  SolarCar SFZ Friedrichshafen, Simplified wiring diagram for iLumen European Solar Challenge. Component symbols are valid.
  48V
  Charger input
  Energy storage pack
  --

custom parts:
  HEZHU BLDC 3-Phase DC motor controller: HEZHU BLDC 3-Phase DC 6V-60V 400W Brushless Motor Controller PWM Hall Motor Control.
  3phase motor with hall sensors: 3phase motor with hall sensors.
  Solar Panel: Renogy 50 Watts 12 Volt Solar Panel
  1 chan 5v relay module: 1 Channel 5V Relay Module Board Shield with Optocoupler Support High and Low Level Trigger for Arduino.
