# Fritzing sketch Solarcar_SFZ_FN_Low_Current_2 (saved by Fritzing 1.0.3b)
breadboards: 1

parts:
  Auxiliary_Battery = DC Power [voltage=12V]
  Left_indicator_light_-_front = LED - 5mm [color="Orange (620nm)" current=0A package="5 mm [THT]"]
  Left_indicator_light_-_tail = LED - 5mm [color="Orange (620nm)" current=0.030A package="5 mm [THT]"]
  Right_indicator_light_-_front = LED - 5mm [color="Orange (620nm)" current=0A package="5 mm [THT]"]
  Right_indicator_light_-_tail = LED - 5mm [color="Orange (620nm)" current=30mA package="5 mm [THT]"]
  Right_indicator_switch = Toggle Switch [package=THT]
  Left_indicator_switch = Toggle Switch [package=THT]
  Flasher_relay1 = npn-Powertransistor [package="TO220 [THT]"]
  Battery_backup_switching_device = X804
  M1 = 1 chan 5v relay module
  Fuse_1A = FUSE [package=fuse_5mm]
  Brake_pedal = SWITCH-MOMENTARY-2 [package=tactile-pth-12mm]
  Hazard_light_switch = Toggle Switch [package=THT]
  D1 = Rectifier Diode [part_number=1N4001 package="Melf DO-213 AB [SMD]"]
  D2 = Rectifier Diode [part_number=1N4001 package="Melf DO-213 AB [SMD]"]
  Instrumentation_and_Telemetry_Computer = Raspberry Pi 4B  # not connected
  ANT1 = Antenna  # not connected
  ANT2 = Antenna  # not connected
  Energy_storage/_BMS = DC Power [voltage=48V]
  DC/_DC_Converter2 = Drok DC buck module
  Left_brake_light = LED - 5mm [color="Red (660nm)" current=0A package="5 mm [THT]"]
  Right_brake_light = LED - 5mm [color="Red (660nm)" current=0A package="5 mm [THT]"]
  Top_brake_light = LED - 5mm [color="Red (660nm)" current=0A package="5 mm [THT]"]
  Fuse_10A = FUSE [package=fuse_5mm]
  Full_beam_switch = Toggle Switch [package=THT]
  Left_full_beam = LED - 5mm [color="White (8000K)" current=0.030A package="5 mm [THT]"]
  Right_full_beam = LED - 5mm [color="White (8000K)" current=0.030A package="5 mm [THT]"]
  Left_dipped_beam = LED - 5mm [color="White (8000K)" current=0.030A package="5 mm [THT]"]
  Right_dipped_beam = LED - 5mm [color="White (8000K)" current=0.030A package="5 mm [THT]"]
  Dipped_beam_switch = Toggle Switch [package=THT]
  Right_front_light = LED - 5mm [color="White (8000K)" current=0.030A package="5 mm [THT]"]
  Left_front_light = LED - 5mm [color="White (8000K)" current=0.030A package="5 mm [THT]"]
  Position_light_switch = Toggle Switch [package=THT]
  Right_tail_light = LED - 5mm [color="Red (660nm)" current=0.030A package="5 mm [THT]"]
  Left_tail_light = LED - 5mm [color="Red (660nm)" current=0.030A package="5 mm [THT]"]
  Horn_button = SWITCH-MOMENTARY-2 [package=tactile-pth-12mm]
  Horn = Piezo Speaker
  R6 = Resistor [tolerance=±5% power=0.25W resistance=0 package=THT]
  R1 = Resistor [tolerance=±5% power=0.25W resistance=0 package=THT]
  R3 = Resistor [tolerance=±5% power=0.25W resistance=0 package=THT]
  R4 = Resistor [tolerance=±5% power=0.25W resistance=0 package=THT]
  R5 = Resistor [tolerance=±5% power=0.25W resistance=0 package=THT]
  R2 = Resistor [tolerance=±5% power=0.25W resistance=0 package=THT]
  Flasher_relay2 = npn-Powertransistor [package="TO220 [THT]"]
  Flashing_green_light = LED - 5mm [color="Green (570nm)" current=0.030A package="5 mm [THT]"]
  DC/_DC_Converter1 = Drok DC buck module
  DC/_DC_Converter3 = Drok DC buck module
  Emergency_electrical_isolation_-_contact2 = Toggle Switch [package=THT]
  Fuse_300A = FUSE [package=fuse_5mm]

nets:
  N1: Auxiliary_Battery.V+, Battery_backup_switching_device.Pin_3, M1.pin_5, DC/_DC_Converter3.Pin_2
  N2: Auxiliary_Battery.V-, Battery_backup_switching_device.Pin_1, Battery_backup_switching_device.Pin_4, Battery_backup_switching_device.Pin_5, M1.pin_2, Energy_storage/_BMS.V-, DC/_DC_Converter2.Pin_1, DC/_DC_Converter2.Pin_4, Left_brake_light.cathode, Right_brake_light.cathode, Top_brake_light.cathode, Horn.pin2, R6.Pin_0, Flashing_green_light.cathode, DC/_DC_Converter1.Pin_1, DC/_DC_Converter3.Pin_1
  N3: Left_indicator_light_-_front.cathode, Left_indicator_light_-_tail.cathode, R1.Pin_0
  N4: Left_indicator_light_-_front.anode, Left_indicator_light_-_tail.anode, Left_indicator_switch.L1, D1.cathode
  N5: Right_indicator_light_-_front.cathode, Right_indicator_light_-_tail.cathode, R2.Pin_0
  N6: Right_indicator_light_-_front.anode, Right_indicator_light_-_tail.anode, Right_indicator_switch.L1, D2.cathode
  N7: Right_indicator_switch.COM, Left_indicator_switch.COM, Flasher_relay1.emitter, Hazard_light_switch.COM
  N8: Flasher_relay1.collector, Fuse_10A.2, Full_beam_switch.COM, Dipped_beam_switch.COM, Position_light_switch.COM, Horn_button.1
  N9: Battery_backup_switching_device.Pin_2, DC/_DC_Converter2.Pin_3
  N10: Battery_backup_switching_device.Pin_6, Fuse_1A.1, Fuse_10A.1
  N11: M1.pin_1, M1.pin_3, Emergency_electrical_isolation_-_contact2.L1
  N12: M1.pin_6, Flasher_relay2.collector
  N13: Fuse_1A.2, Brake_pedal.1
  N14: Brake_pedal.2, Left_brake_light.anode, Right_brake_light.anode, Top_brake_light.anode
  N15: Hazard_light_switch.L1, D1.anode, D2.anode
  N16: Energy_storage/_BMS.V+, Fuse_300A.1
  N17: DC/_DC_Converter2.Pin_2, DC/_DC_Converter1.Pin_2, Emergency_electrical_isolation_-_contact2.COM, Fuse_300A.2
  N18: Full_beam_switch.L1, Left_full_beam.anode, Right_full_beam.anode
  N19: Left_full_beam.cathode, Right_full_beam.cathode, R3.Pin_0
  N20: Left_dipped_beam.cathode, Right_dipped_beam.cathode, R4.Pin_0
  N21: Left_dipped_beam.anode, Right_dipped_beam.anode, Dipped_beam_switch.L1
  N22: Right_front_light.cathode, Left_front_light.cathode, Right_tail_light.cathode, Left_tail_light.cathode, R5.Pin_0
  N23: Right_front_light.anode, Left_front_light.anode, Position_light_switch.L1, Right_tail_light.anode, Left_tail_light.anode
  N24: Horn_button.2, Horn.pin1
  N25: R6.Pin_1, R1.Pin_1, R3.Pin_1, R4.Pin_1, R5.Pin_1, R2.Pin_1
  N26: Flasher_relay2.emitter, Flashing_green_light.anode

notes:
  SIM Card Router
  GPS Module
  Touch Screen
  5V
  48V
  12V
  SolarCar SFZ Friedrichshafen, Simplified wiring diagram for iLumen European Solar Challenge. Component symbols are valid.
  BMS data
  Speed data
  for Driver
  Telemetry data
  Power
  Charge
  --

custom parts:
  X804: This is a power outage automatic switch module for 12V-48V battery.
  1 chan 5v relay module: 1 Channel 5V Relay Module Board Shield with Optocoupler Support High and Low Level Trigger for Arduino.
